# Fritzing sketch Wine Cooler (saved by Fritzing 0.9.3b)
breadboards: 1

parts:
  Temp_Sensor = TMP36 [package=to-92-kit]
  Heatsink_Fan = DC Motor
  Circulation_Fan = DC Motor
  110W_Power_Supply = DC Power [voltage=12V]
  Photon = Photon
  Peltier = Peltier Element
  Peltier_Relay = RELAY [package=relay-t9a-2]
  Circulation_Relay = RELAY [package=relay-t9a-2]

nets:
  VCC: Temp_Sensor.VCC, Photon.3V3
  N1: Temp_Sensor.VOUT, Photon.A0
  GND: Temp_Sensor.GND, Photon.GND, Peltier_Relay.MAIN, Circulation_Relay.MAIN
  N2: Heatsink_Fan.pin_1, Circulation_Fan.pin_1, 110W_Power_Supply.V+, Peltier.pin1
  N3: Heatsink_Fan.pin_2, Peltier.pin2, Peltier_Relay.NO
  N4: Circulation_Fan.pin_2, Circulation_Relay.NO
  N5: Photon.D3, Peltier_Relay.COIL1
  N6: Photon.D4, Circulation_Relay.COIL1
